# Fritzing sketch ledhome_sketch (saved by Fritzing 0.9.0b)
circuit board: 8.46667cm x 5.64444cm
breadboards: 1

parts:
  Part1 = Arduino Nano (Rev3.0)
  Power_for_LEDbar = DC Power [voltage=12V]
  Q1 = Basic FET N-Channel [package="DPak [SMD]"]
  Q2 = Basic FET N-Channel [package="DPak [SMD]"]
  Q3 = Basic FET P-Channel [package="DPak [SMD]"]
  LED1 = RGB LED (com. cathode, rbg) [package="5 mm [THT]"]
  U1 = ENC28J60 [package=ssop28db]

nets (from the schematic view):
  N1: Part1.GND, Power_for_LEDbar.V-, Q1.source, Q2.source, Q3.source, U1.NC
  N2: Part1.D2, U1._INT
  N3: Part1.D3, Q2.Gate
  N4: Part1.D5, Q3.Gate
  N5: Part1.D6, Q1.Gate
  N6: Part1.D10, U1.CS
  N7: Part1.D11/MOSI, U1.SI
  N8: Part1.D12/MISO, U1.SO
  3V3: Part1.3V3, U1.VDD
  N9: Part1.D13/SCK, U1.SCK
  N10: Power_for_LEDbar.V+, LED1.common_cathode
  N11: Q1.drain, LED1.red_anode
  N12: Q2.drain, LED1.blue_anode
  N13: Q3.drain, LED1.green_anode
